# Fritzing sketch schematics (saved by Fritzing 0.9.6b)
breadboards: 1

parts:
  Atmega1 = ATmega328 [package=tqfp]
  U1 = LCD-16X2 [package=lcd-8x2]
  S1 = SWITCH-MOMENTARY-2 [package=tactile_switch_tall]
  R1 = Resistor [tolerance=±5% resistance=220 package="0805 [SMD]"]
  R2 = Resistor [tolerance=±5% resistance=220 package="0805 [SMD]"]
  S2 = SWITCH-MOMENTARY-2 [package=tactile_switch_tall]
  LED1 = smd LED [color="Red (633nm)" package="0603 [SMD]"]
  SG1 = Buzzer 12mm [package=buzzer-ccv]

nets:
  N1: Atmega1.PD4(XCK_T0), U1.DB4
  GND: Atmega1.GND, Atmega1.AGND, U1.VSS, U1.K, S1.2, S2.2, LED1.cathode, SG1.2
  5V: Atmega1.VCC, Atmega1.AVCC, U1.VDD, U1.A, R1.Pin_0
  N2: Atmega1.PD5(T1), U1.DB5
  N3: Atmega1.PD6(AIN0), U1.DB6
  N4: Atmega1.PD7(AIN1), U1.DB7
  N5: Atmega1.PB0(ICP), U1.RS
  N6: Atmega1.PB1(OC1A), U1.E
  N7: Atmega1.PC0(ADC0), S1.1, R1.Pin_1, R2.Pin_1
  N8: Atmega1.PD2(INT0), LED1.anode, SG1.1
  N9: R2.Pin_0, S2.1
